# Fritzing sketch circuit (saved by Fritzing 0.9.10b)

parts:
  HC-SR04_Sensor_1 = HC-SR04 Ultrasonic Distance Sensor
  Part1 = Breakout Board for Electret Microphone
  U5 = SWITCH-SPST-2 [package=r_sw_th]
  U6 = ESP32-38PinWide [part_number=ESP32-38PinWide]
  J2 = Basic Servo
  J3 = Basic Servo
  U4 = WS2812 RGB LED strip
  BATT1 = LiPoly Battery (1300mAh)
  U7 = LM2596 step down module
  D2F1 = D2F-FL Omron Snap Action Limit Switch with Level
  LED8 = LEDs [package=led10mm]
  LED9 = LEDs [package=led10mm]
  LED11 = LEDs [package=led10mm]
  R3 = Trimmer Potentiometer [maximum_resistance=10kΩ knob_status=50% power=0.5W package=THT]

nets:
  VCC: HC-SR04_Sensor_1.VCC, Part1.VCC, U6.VIN, J2.vcc, J3.vcc, U4.VCC, U7.OUT+
  N1: HC-SR04_Sensor_1.TRIG, U6.GPIO12
  N2: HC-SR04_Sensor_1.ECHO, U6.GPIO14
  GND: HC-SR04_Sensor_1.GND, Part1.GND, U6.GPIO11, J3.gnd, U4.GND, BATT1.negative, U7.IN-, U7.OUT-, D2F1.COM
  N3: Part1.AUD, U6.GPIO27
  N4: U5.O, BATT1.positive
  N5: U5.P, U7.IN+
  N6: U6.3.3, R3.leg2
  N7: U6.GPIO32, D2F1.NO
  N8: U6.GPIO33, U4.DIN
  N9: J2.gnd, LED9.A
  N10: LED8.C, LED11.C, R3.leg1
  N11: LED8.A, LED9.C, LED11.A, R3.wiper

custom parts:
  ESP32-38PinWide: Generic 38-Pin ESP32 with wide format (only access to one side of pins on a breadboard) based on Stephen Lilley's HiLetgo ESP-WROOM-32 ESP32 ESP-32S Development Board.
  WS2812 RGB LED strip: WS2812 strip
  LiPoly Battery (1300mAh): Lithium Ion Polymer Battery (1300mAh)
  LM2596 step down module: LM2596 DC-DC step down power supply module 3 A.
  D2F-FL Omron Snap Action Limit Switch with Level: Snap action switch with stainless steel lever.
